// Logisim project ALU.circ as structural Verilog: 1 circuit, main circuit ALU
module ALU (
  input  [31:0] A,
  input  [31:0] B,
  input  [3:0] Op,
  output [31:0] Out,
  output zero,
  output nega
);

  wire comparator_1_lt, comparator_2_lt;
  wire [31:0] add, \and , lui, \nor , \or , slt, sltu, sub, \xor ;

  Adder #(.width(32)) adder_1 (.a(A), .b(B), .out(add));  // open: cin, cout
  Subtractor #(.width(32)) subtractor_1 (.a(A), .b(B), .out(sub));  // open: bin, bout
  assign \and  = A & B;  // AND_Gate and_1, 32 bits wide
  assign \or  = A | B;  // OR_Gate or_1, 32 bits wide
  assign \nor  = ~(A | B);  // NOR_Gate nor_1, 32 bits wide
  assign \xor  = A ^ B;  // XOR_Gate xor_1, 32 bits wide
  Comparator #(.width(32)) comparator_1 (.a(A), .b(B), .lt(comparator_1_lt));  // open: gt, eq
  Shifter #(.width(32)) shifter_1 (.in(B), .\dist (5'b10000), .out(lui));
  Comparator #(.width(32), .mode("unsigned")) comparator_2 (.a(A), .b(B), .lt(comparator_2_lt));  // open: gt, eq
  assign slt = {{31{1'b0}}, comparator_1_lt};  // Bit_Extender bit_extender_1
  assign sltu = {{31{1'b0}}, comparator_2_lt};  // Bit_Extender bit_extender_2
  Multiplexer #(.select(4), .width(32), .disabled(0), .enable("false")) multiplexer_1 (
    .in0(add), .in1(sub), .in2(\and ), .in3(\or ), .in4(\nor ), .in5(\xor ), .in6(slt), .in7(sltu),
    .in8(lui), .out(Out), .sel(Op));  // open: in9, in10, in11, in12, in13, in14, in15
  Pull_Resistor pull_resistor_1 (.node(Out));
  Comparator #(.width(32)) comparator_3 (.a(Out), .b({32{1'b0}}), .eq(zero), .lt(nega));  // open: gt

  // Notes on the sheet:
  //   ALU 算术逻辑单元
endmodule
