// Logisim project CPU.circ as structural Verilog
module CPU (
  input  rst,
  output [31:0] Instr,
  output RegWrite,
  output [4:0] RegAddr,
  output [31:0] RegData,
  output MemWrite,
  output [31:0] MemAddr,
  output [31:0] MemData
);

  wire ALUsrc, and_1_out, and_2_out, Branch, branch_1_isbranch, BRspc, clock_1_out, clock_2_out, clock_3_out,
       DM_ext, EXTop, JmpLnk, JmpSrc, Jump, MemtoReg, negaflg, Shift, SHsrc, zeroflg;
  wire [1:0] DM_size, RegDst;
  wire [2:0] NPCop, SHop;
  wire [3:0] ALUop, BRop;
  wire [4:0] bit_extender_1_out, GRF_A1, GRF_A2, multiplexer_2_out, rd, rt, shamt;
  wire [5:0] funct, op;
  wire [15:0] imm;
  wire [25:0] addr;
  wire [31:0] ALUresult, ALUsrcA, ALUsrcB, DM_WD, ExtImm, multiplexer_4_out, nextPC, PC, PC_4, SHIFTresult;

  Clock clock_1 (.out(clock_1_out));
  PC pc_1 (.nextPC(nextPC), .PC(PC), .clk(clock_1_out), .rst(rst));
  EXT ext_1 (.in(imm), .EXTop(EXTop), .out(ExtImm));
  Branch branch_1 (.branchop(BRop), .ALUzero(zeroflg), .ALUnega(negaflg), .isBranch(branch_1_isbranch));
  and and_1 (and_1_out, Jump, ~JmpSrc);  // AND_Gate
  and and_2 (and_2_out, Jump, JmpSrc);
  IM im_1 (.A(PC), .RD(Instr));
  NPC npc_1 (.PC(PC), .imm16(imm), .addr26(addr), .ra32(ALUsrcA), .op(NPCop), .nextPC(nextPC), .PC4(PC_4));
  Priority_Encoder priority_encoder_1 (
    .in0(1'b1), .in1(branch_1_isbranch), .in2(and_1_out), .in3(and_2_out), .out(NPCop));  // open: in4, in5, in6, in7, en_in, gs, en_out
  IF if_1 (.Instr(Instr), .op(op), .rs(GRF_A1), .rt(rt), .rd(rd), .shamt(shamt), .funct(funct), .imm(imm), .addr(addr));
  ALU alu_1 (.A(ALUsrcA), .B(ALUsrcB), .Op(ALUop), .Out(ALUresult), .zero(zeroflg), .nega(negaflg));
  Multiplexer #(.width(32), .disabled(0), .enable("false")) multiplexer_1 (
    .in0(DM_WD), .in1(ExtImm), .out(ALUsrcB), .sel(ALUsrc));
  Bit_Extender #(.in_width(32), .out_width(5)) bit_extender_1 (.in(ALUsrcA), .out(bit_extender_1_out));
  Multiplexer #(.width(5), .enable("false")) multiplexer_2 (
    .in0(shamt), .in1(bit_extender_1_out), .out(multiplexer_2_out), .sel(SHsrc));
  Multiplexer #(.width(32), .disabled(0), .enable("false")) multiplexer_3 (
    .in0(ALUresult), .in1(SHIFTresult), .out(MemAddr), .sel(Shift));
  Multiplexer #(.width(32), .disabled(0), .enable("false")) multiplexer_4 (
    .in0(MemAddr), .in1(MemData), .out(multiplexer_4_out), .sel(MemtoReg));
  Shifter shifter_1 (.In(DM_WD), .sh(multiplexer_2_out), .op(SHop), .Out(SHIFTresult));
  GRF grf_1 (
    .A1(GRF_A1), .A2(GRF_A2), .A3(RegAddr), .WD(RegData), .RD1(ALUsrcA), .RD2(DM_WD), .clk(clock_2_out),
    .reset(rst), .WE(RegWrite));
  Clock clock_2 (.out(clock_2_out));
  Multiplexer #(.select(2), .width(5), .disabled(0), .enable("false")) multiplexer_5 (
    .in0(rd), .in1(rt), .in2({5{1'b1}}), .out(RegAddr), .sel(RegDst));  // open: in3
  Multiplexer #(.width(32), .disabled(0), .enable("false")) multiplexer_6 (
    .in0(multiplexer_4_out), .in1(PC_4), .out(RegData), .sel(JmpLnk));
  Multiplexer #(.width(5), .disabled(0), .enable("false")) multiplexer_7 (
    .in0(rt), .in1({5{1'b0}}), .out(GRF_A2), .sel(BRspc));
  DM dm_1 (
    .A(MemAddr), .WD(DM_WD), .RD(MemData), .clk(clock_3_out), .rst(rst), .WE(MemWrite), .extop(DM_ext),
    .size(DM_size));
  Clock clock_3 (.out(clock_3_out));
  Control control_1 (
    .opcode(op), .funct(funct), .MemtoReg(MemtoReg), .MemWrite(MemWrite), .ALUop(ALUop), .EXTop(EXTop),
    .ALUsrc(ALUsrc), .RegDst(RegDst), .RegWrite(RegWrite), .BRop(BRop), .Jump(Jump), .JmpSrc(JmpSrc),
    .JmpLnk(JmpLnk), .Branch(Branch), .Msize(DM_size), .Mext(DM_ext), .rs(GRF_A1), .rt(rt), .Shift(Shift),
    .SHop(SHop), .SHsrc(SHsrc), .BRspc(BRspc));

  // Other names for the same wires on the sheet: CALCresult[31:0] = MemAddr; DM_A[31:0] = MemAddr;
  //   DM_RD[31:0] = MemData; GRF_A3[4:0] = RegAddr; GRF_RD1[31:0] = ALUsrcA; GRF_RD2[31:0] = DM_WD;
  //   GRF_WD[31:0] = RegData; rs[4:0] = GRF_A1
endmodule
