// Logisim project Control.circ as structural Verilog: 6 circuits, main circuit Control
module Control (
  input  [5:0] opcode,
  input  [5:0] funct,
  output MemtoReg,
  output MemWrite,
  output RegWrite,
  output [1:0] RegDst,
  output [1:0] Msize,
  output Mext,
  output [3:0] ALUop,
  output EXTop,
  output ALUsrc,
  output Branch,
  output [3:0] BRop,
  output Jump,
  output JmpSrc,
  output JmpLnk
);

  wire add, addi, addu, beq, bne, j, jal, jalr, jr, lb, lbu, lh, lhu, lui, lw, nop, or_4_out, or_5_out,
       or_6_out, orgate_8_1_out, orgate_8_2_out, orgate_8_3_out, orgate_8_5_out, orgate_8_6_out,
       orgate_8_8_out, ori, sb, sh, sub, subu, sw;

  Pull_Resistor pull_resistor_1 (.node(opcode));
  Pull_Resistor pull_resistor_2 (.node(funct));
  instr_judger instr_judger_1 (
    .op(opcode), .op_std({6{1'b0}}), .op_en(1'b1), .funct(funct), .funct_std(6'b100000), .funct_en(1'b1),
    .correct(add));
  instr_judger instr_judger_2 (
    .op(opcode), .op_std({6{1'b0}}), .op_en(1'b1), .funct(funct), .funct_std(6'b100010), .funct_en(1'b1),
    .correct(sub));
  instr_judger instr_judger_3 (
    .op(opcode), .op_std({6{1'b0}}), .op_en(1'b1), .funct(funct), .funct_std(6'b100001), .funct_en(1'b1),
    .correct(addu));
  instr_judger instr_judger_4 (
    .op(opcode), .op_std({6{1'b0}}), .op_en(1'b1), .funct(funct), .funct_std(6'b100011), .funct_en(1'b1),
    .correct(subu));
  instr_judger instr_judger_5 (
    .op(opcode), .op_std(6'b001000), .op_en(1'b1), .funct(funct), .funct_std({6{1'b0}}), .funct_en(1'b0),
    .correct(addi));
  instr_judger instr_judger_6 (
    .op(opcode), .op_std(6'b001111), .op_en(1'b1), .funct(funct), .funct_std({6{1'b0}}), .funct_en(1'b0),
    .correct(lui));
  instr_judger instr_judger_7 (
    .op(opcode), .op_std(6'b001101), .op_en(1'b1), .funct(funct), .funct_std({6{1'b0}}), .funct_en(1'b0),
    .correct(ori));
  orgate_8 orgate_8_1 (.In0(add), .In1(sub), .In2(addu), .In3(subu), .out(orgate_8_1_out));  // open: In4, In5, In6, In7
  orgate_8 orgate_8_2 (
    .In0(addi), .In1(lui), .In2(ori), .In7(MemtoReg), .out(orgate_8_2_out));  // open: In3, In4, In5, In6
  or or_1 (Jump, j, jr, jal, jalr);
  or or_2 (JmpSrc, jr, jalr);
  or or_3 (JmpLnk, jal, jalr);
  orgate_8 orgate_8_3 (
    .In0(add), .In1(sub), .In2(addu), .In3(subu), .In4(addi), .In5(lui), .In6(ori), .out(orgate_8_3_out));  // open: In7
  or or_4 (or_4_out, sw, lw);
  or or_5 (or_5_out, sh, lh, lhu);
  or or_6 (or_6_out, sb, lb, lbu);
  instr_judger instr_judger_8 (
    .op(opcode), .op_std(6'b101011), .op_en(1'b1), .funct(funct), .funct_std({6{1'b0}}), .funct_en(1'b0),
    .correct(sw));
  instr_judger instr_judger_9 (
    .op(opcode), .op_std(6'b100011), .op_en(1'b1), .funct(funct), .funct_std({6{1'b0}}), .funct_en(1'b0),
    .correct(lw));
  instr_judger instr_judger_10 (
    .op(opcode), .op_std(6'b101000), .op_en(1'b1), .funct(funct), .funct_std({6{1'b0}}), .funct_en(1'b0),
    .correct(sb));
  instr_judger instr_judger_11 (
    .op(opcode), .op_std(6'b101001), .op_en(1'b1), .funct(funct), .funct_std({6{1'b0}}), .funct_en(1'b0),
    .correct(sh));
  instr_judger instr_judger_12 (
    .op(opcode), .op_std(6'b100000), .op_en(1'b1), .funct(funct), .funct_std({6{1'b0}}), .funct_en(1'b0),
    .correct(lb));
  instr_judger instr_judger_13 (
    .op(opcode), .op_std(6'b100001), .op_en(1'b1), .funct(funct), .funct_std({6{1'b0}}), .funct_en(1'b0),
    .correct(lh));
  instr_judger instr_judger_14 (
    .op(opcode), .op_std(6'b100100), .op_en(1'b1), .funct(funct), .funct_std({6{1'b0}}), .funct_en(1'b0),
    .correct(lbu));
  instr_judger instr_judger_15 (
    .op(opcode), .op_std(6'b100101), .op_en(1'b1), .funct(funct), .funct_std({6{1'b0}}), .funct_en(1'b0),
    .correct(lhu));
  or or_7 (MemWrite, sw, sb, sh);
  or or_8 (RegWrite, MemtoReg, JmpLnk, orgate_8_3_out);
  Pull_Resistor pull_resistor_3 (.node(RegDst));
  Priority_Encoder #(.select(2), .disabled(0)) priority_encoder_1 (
    .in0(orgate_8_1_out), .in1(orgate_8_2_out), .in2(JmpLnk), .out(RegDst));  // open: in3, gs, en_out, en_in
  Pull_Resistor pull_resistor_4 (.node(Msize));
  Priority_Encoder #(.select(2), .disabled(0)) priority_encoder_2 (
    .in0(or_4_out), .in1(or_5_out), .in2(or_6_out), .out(Msize));  // open: in3, gs, en_out, en_in
  or or_9 (Mext, lb, lh);
  Pull_Resistor pull_resistor_5 (.node(BRop));
  Priority_Encoder #(.select(4)) priority_encoder_3 (
    .in0(1'b0), .in1(beq), .in2(bne), .out(BRop));  // open: in3, in4, in5, in6, in7, in8, in9, in10, in11, in12, in13, in14, in15, gs, en_out, en_in
  instr_judger instr_judger_16 (
    .op(opcode), .op_std({6{1'b0}}), .op_en(1'b1), .funct(funct), .funct_std({6{1'b0}}), .funct_en(1'b1),
    .correct(nop));
  or or_10 (MemtoReg, lw, lb, lh, lbu, lhu);
  orgate_8 orgate_8_4 (.In0(beq), .In1(bne), .out(Branch));  // open: In2, In3, In4, In5, In6, In7
  instr_judger instr_judger_17 (
    .op(opcode), .op_std(6'b000010), .op_en(1'b1), .funct(funct), .funct_std({6{1'b0}}), .funct_en(1'b0),
    .correct(j));
  instr_judger instr_judger_18 (
    .op(opcode), .op_std(6'b000011), .op_en(1'b1), .funct(funct), .funct_std({6{1'b0}}), .funct_en(1'b0),
    .correct(jal));
  instr_judger instr_judger_19 (
    .op(opcode), .op_std({6{1'b0}}), .op_en(1'b1), .funct(funct), .funct_std(6'b001001), .funct_en(1'b1),
    .correct(jalr));
  instr_judger instr_judger_20 (
    .op(opcode), .op_std({6{1'b0}}), .op_en(1'b1), .funct(funct), .funct_std(6'b001000), .funct_en(1'b1),
    .correct(jr));
  instr_judger instr_judger_21 (
    .op(opcode), .op_std(6'b000100), .op_en(1'b1), .funct(funct), .funct_std({6{1'b0}}), .funct_en(1'b0),
    .correct(beq));
  instr_judger instr_judger_22 (
    .op(opcode), .op_std(6'b000101), .op_en(1'b1), .funct(funct), .funct_std({6{1'b0}}), .funct_en(1'b0),
    .correct(bne));
  orgate_8 orgate_8_5 (
    .In0(MemtoReg), .In1(MemWrite), .In2(add), .In3(addu), .In4(addi), .out(orgate_8_5_out));  // open: In5, In6, In7
  orgate_8 orgate_8_6 (.In0(Branch), .In1(subu), .out(orgate_8_6_out));  // open: In2, In3, In4, In5, In6, In7
  orgate_8 orgate_8_7 (
    .In0(MemtoReg), .In1(MemWrite), .In5(addi), .In6(lui), .In7(ori), .out(ALUsrc));  // open: In2, In3, In4
  not not_1 (EXTop, orgate_8_8_out);
  orgate_8 orgate_8_8 (.In0(ori), .out(orgate_8_8_out));  // open: In1, In2, In3, In4, In5, In6, In7
  Pull_Resistor pull_resistor_6 (.node(ALUop));
  Priority_Encoder #(.select(4)) priority_encoder_4 (
    .in1(ori), .in2(orgate_8_5_out), .in3(orgate_8_6_out), .in10(lui), .out(ALUop));  // open: in0, in4, in5, in6, in7, in8, in9, in11, in12, in13, in14, in15, gs, en_out, en_in

  // Notes on the sheet:
  //   Control Unit: CPU的控制器单元
  //   加指令方法：复制一个instr模块，修改opcode和funct的常量以及输出的标签即可
endmodule

module instr_judger (
  input  [5:0] op,
  input  [5:0] op_std,
  input  op_en,
  input  [5:0] funct,
  input  [5:0] funct_std,
  input  funct_en,
  output correct
);

  wire nor_1_out, nor_2_out, or_1_out, or_2_out;
  wire [5:0] xor_1_out, xor_2_out;

  assign xor_1_out = op ^ op_std;  // XOR_Gate xor_1, 6 bits wide
  assign xor_2_out = funct ^ funct_std;  // XOR_Gate xor_2, 6 bits wide
  nor nor_1 (nor_1_out, xor_1_out[0], xor_1_out[1], xor_1_out[2], xor_1_out[3], xor_1_out[4], xor_1_out[5]);
  nor nor_2 (nor_2_out, xor_2_out[0], xor_2_out[1], xor_2_out[2], xor_2_out[3], xor_2_out[4], xor_2_out[5]);
  or or_1 (or_1_out, nor_1_out, ~op_en);  // OR_Gate
  or or_2 (or_2_out, nor_2_out, ~funct_en);  // OR_Gate
  and and_1 (correct, or_1_out, or_2_out);

  // Notes on the sheet:
  //   指令判断器：根据给定的opcode和funct判断一条指令是不是某指令
  //   op: 输入指令的op，op_std: 要判断是不是的指令的op，op_en: 是否检查op一致
  //   输出：是否为某指令
  //   例如：将op_std设定为0，funct_std设定为100000，若输入的op和funct一致则该指令为add指令
  //   下面的funct同理
  //   使用方法：op以及funct连接模块输入的op和funct
  //   两路en信号是以备万一某些指令只有op确定而funct任意，可以不判断funct
  //   op_std, funct_std用常量
  //   （例如I型和J型指令，funct对应的位数都是立即数，没意义）
endmodule

module big_andgate_32 (
  input  in_1,
  input  in_2,
  input  in_3,
  input  in_4,
  input  in_5,
  input  in_6,
  input  in_7,
  input  in_8,
  input  in_9,
  input  in_10,
  input  in_11,
  input  in_12,
  input  in_13,
  input  in_14,
  input  in_15,
  input  in_16,
  input  in_17,
  input  in_18,
  input  in_19,
  input  in_20,
  input  in_21,
  input  in_22,
  input  in_23,
  input  in_24,
  input  in_25,
  input  in_26,
  input  in_27,
  input  in_28,
  input  in_29,
  input  in_30,
  input  in_31,
  input  in_32,
  output out_33
);

  Pull_Resistor pull_resistor_1 (.node(in_1));
  Pull_Resistor pull_resistor_2 (.node(in_9));
  Pull_Resistor pull_resistor_3 (.node(in_17));
  Pull_Resistor pull_resistor_4 (.node(in_25));
  Pull_Resistor pull_resistor_5 (.node(in_2));
  Pull_Resistor pull_resistor_6 (.node(in_10));
  Pull_Resistor pull_resistor_7 (.node(in_18));
  Pull_Resistor pull_resistor_8 (.node(in_26));
  Pull_Resistor pull_resistor_9 (.node(in_3));
  Pull_Resistor pull_resistor_10 (.node(in_11));
  Pull_Resistor pull_resistor_11 (.node(in_19));
  Pull_Resistor pull_resistor_12 (.node(in_27));
  Pull_Resistor pull_resistor_13 (.node(in_4));
  Pull_Resistor pull_resistor_14 (.node(in_12));
  Pull_Resistor pull_resistor_15 (.node(in_20));
  Pull_Resistor pull_resistor_16 (.node(in_28));
  Pull_Resistor pull_resistor_17 (.node(in_6));
  Pull_Resistor pull_resistor_18 (.node(in_5));
  Pull_Resistor pull_resistor_19 (.node(in_13));
  Pull_Resistor pull_resistor_20 (.node(in_14));
  Pull_Resistor pull_resistor_21 (.node(in_21));
  Pull_Resistor pull_resistor_22 (.node(in_22));
  Pull_Resistor pull_resistor_23 (.node(in_29));
  Pull_Resistor pull_resistor_24 (.node(in_30));
  Pull_Resistor pull_resistor_25 (.node(in_7));
  Pull_Resistor pull_resistor_26 (.node(in_15));
  Pull_Resistor pull_resistor_27 (.node(in_23));
  Pull_Resistor pull_resistor_28 (.node(in_31));
  Pull_Resistor pull_resistor_29 (.node(in_8));
  Pull_Resistor pull_resistor_30 (.node(in_16));
  Pull_Resistor pull_resistor_31 (.node(in_24));
  Pull_Resistor pull_resistor_32 (.node(in_32));
  and and_1 (out_33, in_1, in_2, in_3, in_4, in_5, in_6, in_7, in_8, in_9, in_10, in_11, in_12, in_13, in_14, in_15, in_16, in_17, in_18, in_19, in_20, in_21, in_22, in_23, in_24, in_25, in_26, in_27, in_28, in_29, in_30, in_31, in_32);

  // Notes on the sheet:
  //   在控制单元这里定制的专用与门，自带32路1位输入，所有的X输入自动下拉为0，不影响有输入的端。全X则输出0
endmodule

module big_orgate_32 (
  input  in_1,
  input  in_2,
  input  in_3,
  input  in_4,
  input  in_5,
  input  in_6,
  input  in_7,
  input  in_8,
  input  in_9,
  input  in_10,
  input  in_11,
  input  in_12,
  input  in_13,
  input  in_14,
  input  in_15,
  input  in_16,
  input  in_17,
  input  in_18,
  input  in_19,
  input  in_20,
  input  in_21,
  input  in_22,
  input  in_23,
  input  in_24,
  input  in_25,
  input  in_26,
  input  in_27,
  input  in_28,
  input  in_29,
  input  in_30,
  input  in_31,
  input  in_32,
  output out_33
);

  Pull_Resistor pull_resistor_1 (.node(in_1));
  Pull_Resistor pull_resistor_2 (.node(in_9));
  Pull_Resistor pull_resistor_3 (.node(in_17));
  Pull_Resistor pull_resistor_4 (.node(in_25));
  Pull_Resistor pull_resistor_5 (.node(in_2));
  Pull_Resistor pull_resistor_6 (.node(in_10));
  Pull_Resistor pull_resistor_7 (.node(in_18));
  Pull_Resistor pull_resistor_8 (.node(in_26));
  Pull_Resistor pull_resistor_9 (.node(in_3));
  Pull_Resistor pull_resistor_10 (.node(in_11));
  Pull_Resistor pull_resistor_11 (.node(in_19));
  Pull_Resistor pull_resistor_12 (.node(in_27));
  Pull_Resistor pull_resistor_13 (.node(in_4));
  Pull_Resistor pull_resistor_14 (.node(in_12));
  Pull_Resistor pull_resistor_15 (.node(in_20));
  Pull_Resistor pull_resistor_16 (.node(in_28));
  Pull_Resistor pull_resistor_17 (.node(in_6));
  Pull_Resistor pull_resistor_18 (.node(in_5));
  Pull_Resistor pull_resistor_19 (.node(in_13));
  Pull_Resistor pull_resistor_20 (.node(in_14));
  Pull_Resistor pull_resistor_21 (.node(in_21));
  Pull_Resistor pull_resistor_22 (.node(in_22));
  Pull_Resistor pull_resistor_23 (.node(in_29));
  Pull_Resistor pull_resistor_24 (.node(in_30));
  Pull_Resistor pull_resistor_25 (.node(in_7));
  Pull_Resistor pull_resistor_26 (.node(in_15));
  Pull_Resistor pull_resistor_27 (.node(in_23));
  Pull_Resistor pull_resistor_28 (.node(in_31));
  Pull_Resistor pull_resistor_29 (.node(in_8));
  Pull_Resistor pull_resistor_30 (.node(in_16));
  Pull_Resistor pull_resistor_31 (.node(in_24));
  Pull_Resistor pull_resistor_32 (.node(in_32));
  or or_1 (out_33, in_1, in_2, in_3, in_4, in_5, in_6, in_7, in_8, in_9, in_10, in_11, in_12, in_13, in_14, in_15, in_16, in_17, in_18, in_19, in_20, in_21, in_22, in_23, in_24, in_25, in_26, in_27, in_28, in_29, in_30, in_31, in_32);

  // Notes on the sheet:
  //   在控制单元这里定制的专用或门，自带32路1位输入，所有的X输入自动下拉为0，不影响有输入的端。全X则输出0
endmodule

module andgate_8 (
  input  In0,
  input  In1,
  input  In2,
  input  In3,
  input  In4,
  input  In5,
  input  In6,
  input  In7,
  output out
);

  Pull_Resistor pull_resistor_1 (.node(In0));
  Pull_Resistor pull_resistor_2 (.node(In1));
  Pull_Resistor pull_resistor_3 (.node(In5));
  Pull_Resistor pull_resistor_4 (.node(In2));
  Pull_Resistor pull_resistor_5 (.node(In4));
  Pull_Resistor pull_resistor_6 (.node(In3));
  Pull_Resistor pull_resistor_7 (.node(In6));
  Pull_Resistor pull_resistor_8 (.node(In7));
  and and_1 (out, In0, In1, In2, In3, In4, In5, In6, In7);
endmodule

module orgate_8 (
  input  In0,
  input  In1,
  input  In2,
  input  In3,
  input  In4,
  input  In5,
  input  In6,
  input  In7,
  output out
);

  Pull_Resistor pull_resistor_1 (.node(In1));
  Pull_Resistor pull_resistor_2 (.node(In0));
  Pull_Resistor pull_resistor_3 (.node(In2));
  Pull_Resistor pull_resistor_4 (.node(In3));
  Pull_Resistor pull_resistor_5 (.node(In5));
  Pull_Resistor pull_resistor_6 (.node(In4));
  Pull_Resistor pull_resistor_7 (.node(In7));
  Pull_Resistor pull_resistor_8 (.node(In6));
  or or_1 (out, In0, In1, In2, In3, In4, In5, In6, In7);
endmodule
