// Logisim project DM.circ as structural Verilog: 2 circuits, main circuit DM
module DM (
  input  clk,
  input  rst,
  input  WE,
  input  [31:0] A,
  input  [31:0] WD,
  output [31:0] RD
);

  wire [23:0] dm_addr_1_addr24;

  // Probe on A
  // Probe on WD
  dm_addr dm_addr_1 (.Addr32(A), .Addr24(dm_addr_1_addr24));
  RAM #(.addrWidth(24), .dataWidth(32), .bus("separate")) ram_1 (
    .addr(dm_addr_1_addr24), .din(WD), .data(RD), .str(WE), .sel(1'b1), .clk(clk), .ld(1'b1), .clr(rst));

  // Notes on the sheet:
  //   Data Memory 数据存储器
endmodule

module dm_addr (
  input  [31:0] Addr32,
  output [23:0] Addr24
);

  wire [31:0] shifter_1_out;

  Shifter #(.width(32), .shift("lr")) shifter_1 (.in(Addr32), .\dist (5'b00010), .out(shifter_1_out));
  Bit_Extender #(.in_width(32), .out_width(24)) bit_extender_1 (.in(shifter_1_out), .out(Addr24));

  // Notes on the sheet:
  //   dm_addr: 将DM的32位输入地址转化成24位的RAM地址
endmodule
