// Logisim project Shifter.circ as structural Verilog: 1 circuit, main circuit Shifter
module Shifter (
  input  [31:0] In,
  input  [4:0] sh,
  input  [2:0] op,
  output [31:0] Out
);

  wire [31:0] aright, lleft, lright, rleft, rright;

  Shifter_part #(.width(32)) shifter_1 (.in(In), .\dist (sh), .out(lleft));
  Shifter_part #(.width(32), .shift("lr")) shifter_2 (.in(In), .\dist (sh), .out(lright));
  Shifter_part #(.width(32), .shift("ar")) shifter_3 (.in(In), .\dist (sh), .out(aright));
  Shifter_part #(.width(32), .shift("rl")) shifter_4 (.in(In), .\dist (sh), .out(rleft));
  Shifter_part #(.width(32), .shift("rr")) shifter_5 (.in(In), .\dist (sh), .out(rright));
  Multiplexer #(.select(3), .width(32), .disabled(0), .enable("false")) multiplexer_1 (
    .in0(lleft), .in1(lright), .in2(aright), .in3(rleft), .in4(rright), .out(Out), .sel(op));  // open: in5, in6, in7
  Pull_Resistor pull_resistor_1 (.node(Out));

  // Notes on the sheet:
  //   移位器：In 32位输入，sh 5位输入-移位的数目，op 3位 操作种类
  //   op对应的操作种类： 000:左移，001:逻辑右移，010:算术右移，011:循环左移，100: 循环右移
endmodule
